# Fritzing sketch SmaryLock (saved by Fritzing 0.9.0b)
breadboards: 1

parts:
  R2 = Resistor [tolerance=±5% resistance=10k package=THT]
  S1 = Pushbutton [package="[THT]"]
  S2 = Pushbutton [package="[THT]"]
  R1 = Resistor [tolerance=±5% resistance=10k package=THT]
  VCC = 4 x AAA Battery Mount
  J1 = Basic Servo

nets:
  GND: R2.Pin_0, R1.Pin_1, VCC.-, J1.gnd
  A3: R2.Pin_1, S2.Pin_1, S2.Pin_2
  V33: S1.Pin_1, S1.Pin_2, S2.Pin_4
  A2: S1.Pin_4, R1.Pin_0
  A1/VIN: VCC.+, J1.vcc, J1.pulse
